# Fritzing sketch SmartSwitch (saved by Fritzing 0.9.8b)

parts:
  U1 = NodeMCU V3.0
  TTP223B1 = TTP223B Capacitive Touch Sensor Module
  TTP223B2 = TTP223B Capacitive Touch Sensor Module
  J1 = Generic male header - 4 pins [form="♂ (male)" package=THT]
  元件1 = IFR520 MOS module [package=THT]
  元件2 = IFR520 MOS module [package=THT]
  元件3 = Ambient Light Sensor (TEMT6000 Breakout Board)
  PCB2 = RTC_DS1302_module

nets:
  N1: U1.D0, 元件1.SIG
  N2: U1.D1, TTP223B1.SIG
  N3: U1.D2, 元件2.SIG
  N4: U1.D3, J1.IN1
  N5: U1.D4, J1.IN2
  VCC: U1.3V3, TTP223B1.VCC, TTP223B2.VCC, J1.VCC, 元件1.VCC, 元件2.VCC, 元件3.VCC, PCB2.VCC
  GND: U1.GND, TTP223B1.GND, TTP223B2.GND, J1.GND, 元件1.GND, 元件2.GND, 元件3.GND, PCB2.GND
  N6: U1.D5, PCB2.RST
  N7: U1.D6, PCB2.DAT
  N8: U1.D7, PCB2.CLK
  N9: U1.D8, TTP223B2.SIG
  N10: U1.A0, 元件3.S

custom parts:
  NodeMCU V3.0: NodeMcu V3 Lua WIFI Development Board
  TTP223B Capacitive Touch Sensor Module: The TTP223B capacitive touch sensor module uses the TTP223B IC. The appropriate voltage is approximately 2 to 5.5 volts.
  Generic male header - 4 pins: Generic male header
  RTC_DS1302_module: Arduino module DS1302 SPI Real Time Clock
